# Fritzing sketch MapuaCapstoneFritzing (saved by Fritzing 0.8.7b)

parts:
  Part1 = Arduino Mega 2560 (Rev3)
  U1 = RFID RC522 SIP - 8 pins [chip_label="RFID RC522" package="SIP (Single Inline) [THT]"]
  U2 = ESP8266 WiFi Module [part_number=ESP8266]
  Display1 = LCD screen 16x2 IIC [part_number=101290]
  SD_card_module1 = SD Card Module
  S1 = SWITCH-MOMENTARY-2 [package=tactile-pth-12mm]
  S2 = SWITCH-MOMENTARY-2 [package=tactile-pth-12mm]
  S3 = SWITCH-MOMENTARY-2 [package=tactile-pth-12mm]
  S4 = SWITCH-MOMENTARY-2 [package=tactile-pth-12mm]
  S5 = SWITCH-MOMENTARY-2 [package=tactile-pth-12mm]

nets:
  N1: Part1.D21/SCL, Display1.SCL
  N2: Part1.D20/SDA, Display1.SDA
  N3: Part1.D19/RX1, U2.TXD
  N4: Part1.D18/TX1, U2.RXD
  GND: Part1.GND, Display1.GND, SD_card_module1.GND
  3V3: Part1.3V3, U2.VCC
  VCC: Part1.5V, U1.VCC, Display1.VCC, SD_card_module1.+5
  N5: Part1.D23, S1.1
  N6: Part1.D25, S2.1
  N7: Part1.D27, S3.1
  N8: Part1.D29, S4.1
  N9: Part1.D31, S5.1
  N10: Part1.D43, SD_card_module1.CS
  N11: Part1.D48, U1.RST
  N12: Part1.D50, SD_card_module1.MISO
  N13: Part1.D51, SD_card_module1.MOSI
  N14: Part1.D52, SD_card_module1.SCK

custom parts:
  RFID RC522 SIP - 8 pins: A SIP stand-in part for RFID RC522 . With 8 pins on a 300 mil single inline package (SIP) footprint.
  ESP8266 WiFi Module: Generic WiFi Module based on the ESP8266 with onboard PCB antenna and UART communications
  LCD screen 16x2 IIC: LCD screen with HD44780 controller enables showing text, symbols, value or anything else that comes from Croduino/Arduino. It is capable of showing 16 symbols in two lines and therefore can be used in many projects that need to send clearly visible and legible output information.. • Color of symbols: White • Backlight: Blue • Dimensions: 80 x 36 x 12 mm • Screen dimensions: 64.5 x 16 mm •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
  SD Card Module: SD Card Module Slot Socket Reader For Arduino ARM MCU
