# Fritzing sketch client_wiring (saved by Fritzing 0.8.7b)

parts:
  Part1 = NRF24L01
  U1 = atmega328 [package=dip]
  BAT1 = Battery Holders [package=battcom_20mm_pth]
  XTAL1 = Crystal [frequency="16 Mhz" package=THT]
  C1 = Capacitor [package=cap-pth-small2]
  C2 = Capacitor [package=cap-pth-small2]
  U2 = Vibration Motor- ROB-08449 [package=vibe-motor-10mm]
  S1 = SWITCH-MOMENTARY-2 [package=tactile-pth-12mm]
  R1 = Resistor [tolerance=±5% resistance=10k package=THT]
  C3 = Capacitor [package=cap-pth-small2]

nets:
  N1: Part1.MOSI, U1.D12
  N2: Part1.CSN, U1.D10_(PWM)
  VCC: Part1.VCC, U1.VCC, BAT1.+, R1.Pin_1, C3.2
  N3: Part1.MISO, U1.D11_(PWM)
  N4: Part1.SCK, U1.D13
  N5: Part1.CE, U1.D9_(PWM)
  GND: Part1.GND, U1.GND, BAT1.-, C1.1, C2.1, U2.+, S1.2, C3.1
  N6: U1.D2, S1.1, R1.Pin_0
  N7: U1.D3_(PWM), U2.-
  N8: U1.XLAT1, XTAL1.pin_1, C1.2
  N9: U1.XLAT2, XTAL1.pin_0, C2.2
