# Fritzing sketch server_wiring (saved by Fritzing 0.8.7b)

parts:
  Part1 = NRF24L01
  Part2 = Arduino Micro (Rev3)
  Part3 = OLED Monochrome 128x64 0.96 inch [part_number=326]
  S4 = SWITCH-MOMENTARY-2 [package=tactile-pth-12mm]
  LED1 = LED - 5mm [color="Red (633nm)" package="5 mm [THT]"]
  J1 = Piezo Speaker
  R1 = Resistor [tolerance=±5% resistance=220 package=THT]
  R2 = Resistor [tolerance=±5% resistance=10k package=THT]

nets:
  N1: Part1.MOSI, Part2.D11_PWM
  N2: Part1.CSN, Part2.D10_PWM/A10
  VCC: Part1.VCC, Part2.3V3
  N3: Part1.MISO, Part2.D12_PWM/A11
  N4: Part1.SCK, Part2.D13_PWM
  N5: Part1.CE, Part2.D9_PWM/A9
  GND: Part1.GND, Part2.GND, S4.1, J1.pin1
  N6: Part2.D2/SDA, S4.2, R2.Pin_1
  N7: Part2.D3/SCL, J1.pin2
  5V: Part2.5V, Part3.VIN, R1.Pin_0, R2.Pin_0
  N8: Part2.A5, Part3.SCLK_SCK
  N9: Part2.A4, Part3.MOSI_SDA
  N10: Part3.GND, LED1.cathode
  N11: LED1.anode, R1.Pin_1

custom parts:
  OLED Monochrome 128x64 0.96 inch: These displays are small, only about 1" diameter, but very readable due to the high contrast of an OLED display. This display is made of 128x64 individual white OLED pixels, each one is turned on or off by the controller chip. Because the display makes its own light, no backlight is required. This reduces the power required to run the OLED and is why the display has such high contrast; we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
