# Fritzing sketch TechnoVairSchematic (saved by Fritzing 0.8.7b)

parts:
  Part1 = MQ-3 breakout
  Part2 = Arduino Mega ADK (Rev3)
  Display1 = LCD screen 16x2 IIC [part_number=101290]

nets:
  VCC: Part1.VCC, Part2.5V, Display1.VCC
  GND: Part1.GND, Part2.GND, Display1.GND
  N1: Part1.DO, Part2.D2_PWM
  N2: Part1.AO, Part2.A0
  N3: Part2.D21/SCL, Display1.SCL
  N4: Part2.D20/SDA, Display1.SDA

custom parts:
  MQ-3 breakout: Alcohol sensor is capable of detecting alcohol (ethanol) particles on itself and gives the information in digital form back to us to manipulate with it. SKU:101251 • Voltage: 5V DC • Power: max 750mW • Measurement range: 0.04-4mg/L
  LCD screen 16x2 IIC: LCD screen with HD44780 controller enables showing text, symbols, value or anything else that comes from Croduino/Arduino. It is capable of showing 16 symbols in two lines and therefore can be used in many projects that need to send clearly visible and legible output information.. • Color of symbols: White • Backlight: Blue • Dimensions: 80 x 36 x 12 mm • Screen dimensions: 64.5 x 16 mm •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
