# Fritzing sketch Capstone_BPWCB (saved by Fritzing 0.8.7b)

parts:
  U1 = NEO 6M GPS
  Part1 = Arduino Mega 2560 (Rev3)
  Part2 = Adafruit FONA - Mini Cellular GSM Breakout
  Keyes1 = Keyes IR Infrared Sensor Switch Module
  U3 = HC-SR04 [chip_label=IC package="SIP (Single Inline) [THT]"]
  S1 = H-Bridge with L298N
  S2 = H-Bridge with L298N
  M1 = DC Motor
  M2 = DC Motor
  M3 = DC Motor
  J1 = Basic Servo
  GY1 = GY-521 (MPU-6050) [form="♀ (female)" package=THT]
  LED1 = LED - 5mm [color="Green (570nm)" package="5 mm [THT]"]
  R1 = Resistor [tolerance=±5% resistance=220 package=THT]
  S4 = SWITCH-MOMENTARY-2 [package=tactile-pth-12mm]
  R2 = Resistor [tolerance=±5% resistance=10k package=THT]
  U4 = LIPO-110mAh [package=lipo-110]
  Reg1 = DC-DC CONVERTER [part_number=80633 package=dc-dc_converter]
  R3 = Resistor [tolerance=±5% resistance=10k package=THT]
  R4 = Resistor [tolerance=±5% resistance=10k package=THT]

nets:
  N1: U1.RXD, Part1.D18/TX1
  N2: U1.TXD, Part1.D19/RX1
  GND: U1.GND, Part1.GND, Part2.GND, Keyes1.GND, U3.GND, J1.gnd, GY1.pin2, Reg1.OUT-
  VCC: U1.VCC, Part1.5V, Part2.VBAT, Keyes1.VCC, U3.Vcc, J1.vcc, GY1.pin1, R1.Pin_0
  N3: Part1.A8, S4.2, R2.Pin_0
  N4: Part1.A1, R4.Pin_1
  N5: Part1.A7, LED1.cathode
  N6: Part1.D21/SCL, GY1.pin3
  N7: Part1.D20/SDA, GY1.pin4
  N8: Part1.D11_PWM, Part2.RXD_5V
  N9: Part1.D10_PWM, Part2.TXD_5V
  5V: Part1.VIN, S1.5V, S2.5V, Reg1.OUT+
  N10: Part1.D2_PWM, U3.Echo
  N11: Part1.D3_PWM, U3.Trig
  N12: Part1.D4_PWM, J1.pulse
  N13: Part1.D5_PWM, S2.ENA
  N14: Part1.D6_PWM, S1.ENA
  N15: Part1.D7_PWM, S1.ENB
  N16: Part1.D22, Keyes1.EN
  N17: Part1.D23, Keyes1.out
  N18: Part1.D48, S2.IN2
  N19: Part1.D49, S2.IN1
  N20: Part1.D50, S1.IN4
  N21: Part1.D51, S1.IN1
  N22: Part1.D52, S1.IN3
  N23: Part1.D53, S1.IN2
  N24: S1.M1-01, M2.pin_2
  N25: S1.M1-02, M2.pin_1
  N26: S1.M2-01, M1.pin_2
  N27: S1.M2-02, M1.pin_1
  N28: S2.GND, S4.1
  N29: S2.M1-01, M3.pin_2
  N30: S2.M1-02, M3.pin_1
  N31: LED1.anode, R1.Pin_1, R2.Pin_1
  N32: U4.+, Reg1.IN+, R4.Pin_0
  N33: U4.-, Reg1.IN-, R3.Pin_1

custom parts:
  NEO 6M GPS: uSD module
  Adafruit FONA - Mini Cellular GSM Breakout: An all-in-one cellular phone module that lets you add voice, text, SMS and GPRS data to your project. Quad-band 850/900/1800/1900MHz - connect onto any global GSM network with any 2G SIM. Includes an onboard LiPoly battery charging circuitry so you can take your project on the go. Also works as an FM radio receiver.
  Keyes IR Infrared Sensor Switch Module: An infrared obstacle detector
  HC-SR04: HC-SR04 ultrasound distance sensor
  H-Bridge with L298N: h-bridge
  GY-521 (MPU-6050): Placa GY-521 basada en conjunto de acelerómetro+giroscopios MPU-6050
  DC-DC CONVERTER: WYHP 5A constant current/voltage manufactured by Shenzhen Weiyapuhua Technology Co., Ltd
