# Fritzing sketch FishFeederSchematic (saved by Fritzing 0.8.7b)

parts:
  A1 = A4988
  S1 = H-Bridge with L298N
  M1 = Stepper Motor - Bipolar
  Keyes1 = Keyes IR Infrared Sensor Switch Module
  U4 = HC-SR04 [chip_label=IC package="SIP (Single Inline) [THT]"]
  S2 = Round Pushbutton
  S3 = Round Pushbutton
  S4 = Round Pushbutton
  M2 = DC Motor
  M3 = DC Motor
  U5 = POT [package=pot_alpha_rv16af-20]
  U6 = POT [package=pot_alpha_rv16af-20]
  Reg1 = DC-DC CONVERTER [part_number=80633 package=dc-dc_converter]
  U7 = LIPO-2000mAh [package=lipo-2000]
  Display1 = LCD screen 16x2 IIC [part_number=101290]
  Part1 = Arduino Uno (Rev3)
  R1 = Resistor [tolerance=±5% resistance=220 package=THT]
  LED1 = LED - 5mm [color="Red (633nm)" package="5 mm [THT]"]
  LED2 = LED - 5mm [color="Red (633nm)" package="5 mm [THT]"]
  Part2 = Micro Lipo Charger

nets:
  GND: A1.GND, S1.GND, Keyes1.GND, U4.GND, S2.leg0, S3.leg0, S4.leg0, U5.A, U6.A, Display1.GND, Part1.GND
  VCC: A1.VDD, S1.5V, S1.ENA, S1.ENB, Keyes1.VCC, U4.Vcc, U5.E, U6.E, Display1.VCC, Part1.5V, R1.Pin_1
  N1: A1.1B, M1.D
  N2: A1.1A, M1.B
  N3: A1.2A, M1.C
  N4: A1.2B, M1.A
  N5: A1.DIRECTION, Part1.D4
  N6: A1.STEP, Part1.D3_PWM
  N7: A1.SLEEP, A1.RESET
  12V: S1.12V, Reg1.OUT+, Part1.VIN
  N8: S1.IN1, Part1.D8
  N9: S1.IN2, Part1.D9_PWM
  N10: S1.IN3, Part1.D10_PWM/SS
  N11: S1.IN4, Part1.D11_PWM/MOSI
  N12: S1.M1-01, M3.pin_2
  N13: S1.M1-02, M3.pin_1
  N14: S1.M2-01, M2.pin_2
  N15: S1.M2-02, M2.pin_1
  N16: Keyes1.out, Part1.D2
  N17: U4.Trig, Part1.D6_PWM
  N18: U4.Echo, Part1.D5_PWM
  N19: S2.leg1, Part1.D12/MISO
  N20: S3.leg1, Reg1.OUT-
  N21: S4.leg1, Part1.D13/SCK
  N22: U5.S, Part1.A0
  N23: U6.S, Part1.A1
  N24: Reg1.IN-, U7.-, Part2.GND
  N25: Reg1.IN+, U7.+, Part2.VBAT
  N26: Display1.SDA, Part1.A4/SDA
  N27: Display1.SCL, Part1.A5/SCL
  N28: Part1.D7, LED1.cathode, LED2.cathode
  N29: R1.Pin_0, LED1.anode, LED2.anode

custom parts:
  H-Bridge with L298N: h-bridge
  Keyes IR Infrared Sensor Switch Module: An infrared obstacle detector
  HC-SR04: HC-SR04 ultrasound distance sensor
  DC-DC CONVERTER: WYHP 5A constant current/voltage manufactured by Shenzhen Weiyapuhua Technology Co., Ltd
  LCD screen 16x2 IIC: LCD screen with HD44780 controller enables showing text, symbols, value or anything else that comes from Croduino/Arduino. It is capable of showing 16 symbols in two lines and therefore can be used in many projects that need to send clearly visible and legible output information.. • Color of symbols: White • Backlight: Blue • Dimensions: 80 x 36 x 12 mm • Screen dimensions: 64.5 x 16 mm •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
  Micro Lipo Charger: Oh so handy, this little lipo charger is so small and easy to use you can keep it on your desk or mount it easily into any project! Simply plug it via any MicroUSB cable into a USB port and a 3.7V/4.2V lithium polymer or lithium ion rechargeable battery into the JST plug on the other end. There are two LEDs - one red and one green. While charging, the red LED is lit. When the battery is fully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
