# Fritzing sketch PillDispenser_Schematic (saved by Fritzing 0.8.7b)

parts:
  Part1 = Arduino Mega 2560 (Rev3)
  L1 = Solenoid
  Q1 = Basic FET N-Channel [package="TO220 [THT]"]
  R1 = Resistor [tolerance=±5% resistance=10k package=THT]
  L2 = Solenoid
  Q2 = Basic FET N-Channel [package="TO220 [THT]"]
  L3 = Solenoid
  L4 = Solenoid
  R3 = Resistor [tolerance=±5% resistance=10k package=THT]
  L5 = Solenoid
  L6 = Solenoid
  Q5 = Basic FET N-Channel [package="TO220 [THT]"]
  Q6 = Basic FET N-Channel [package="TO220 [THT]"]
  R5 = Resistor [tolerance=±5% resistance=10k package=THT]
  R6 = Resistor [tolerance=±5% resistance=10k package=THT]
  L7 = Solenoid
  L8 = Solenoid
  L9 = Solenoid
  L10 = Solenoid
  L11 = Solenoid
  L12 = Solenoid
  Q7 = Basic FET N-Channel [package="TO220 [THT]"]
  Q8 = Basic FET N-Channel [package="TO220 [THT]"]
  Q9 = Basic FET N-Channel [package="TO220 [THT]"]
  Q10 = Basic FET N-Channel [package="TO220 [THT]"]
  Q11 = Basic FET N-Channel [package="TO220 [THT]"]
  Q12 = Basic FET N-Channel [package="TO220 [THT]"]
  R7 = Resistor [tolerance=±5% resistance=10k package=THT]
  R8 = Resistor [tolerance=±5% resistance=10k package=THT]
  R9 = Resistor [tolerance=±5% resistance=10k package=THT]
  R10 = Resistor [tolerance=±5% resistance=10k package=THT]
  R11 = Resistor [tolerance=±5% resistance=10k package=THT]
  R12 = Resistor [tolerance=±5% resistance=10k package=THT]
  R2 = Resistor [tolerance=±5% resistance=10k package=THT]
  Q4 = Basic FET N-Channel [package="TO220 [THT]"]
  Q3 = Basic FET N-Channel [package="TO220 [THT]"]
  R4 = Resistor [tolerance=±5% resistance=10k package=THT]
  CNY70-1 = CNY70 [package=cny70-side]
  R13 = Resistor [tolerance=±5% resistance=220 package=THT]
  CNY70-2 = CNY70 [package=cny70-side]
  R14 = Resistor [tolerance=±5% resistance=220 package=THT]
  CNY70-3 = CNY70 [package=cny70-side]
  CNY70-4 = CNY70 [package=cny70-side]
  R15 = Resistor [tolerance=±5% resistance=220 package=THT]
  R16 = Resistor [tolerance=±5% resistance=220 package=THT]
  CNY70-5 = CNY70 [package=cny70-side]
  CNY70-6 = CNY70 [package=cny70-side]
  R17 = Resistor [tolerance=±5% resistance=220 package=THT]
  R18 = Resistor [tolerance=±5% resistance=220 package=THT]
  R19 = Resistor [tolerance=±5% resistance=10k package=THT]
  R20 = Resistor [tolerance=±5% resistance=10k package=THT]
  R21 = Resistor [tolerance=±5% resistance=10k package=THT]
  R22 = Resistor [tolerance=±5% resistance=10k package=THT]
  R23 = Resistor [tolerance=±5% resistance=10k package=THT]
  R24 = Resistor [tolerance=±5% resistance=10k package=THT]
  J1 = Piezo Speaker
  S1 = SWITCH-MOMENTARY-2 [package=tactile-pth-12mm]
  S2 = SWITCH-MOMENTARY-2 [package=tactile-pth-12mm]
  S3 = SWITCH-MOMENTARY-2 [package=tactile-pth-12mm]
  S4 = SWITCH-MOMENTARY-2 [package=tactile-pth-12mm]
  Part2 = Adafruit DS3231 [part_number="Adafruit #3013"]
  Display1 = LCD screen 16x2 IIC [part_number=101290]
  LED1 = LED - 5mm [color="Red (633nm)" package="5 mm [THT]"]
  R25 = Resistor [tolerance=±5% resistance=220 package=THT]
  Reg1 = DC-DC CONVERTER [part_number=80633 package=dc-dc_converter]
  U1 = LIPO-2000mAh [package=lipo-2000]
  Part3 = Micro Lipo Charger

nets:
  N1: Part1.A0, CNY70-1.C, R19.Pin_1
  N2: Part1.A1, CNY70-2.C, R20.Pin_1
  N3: Part1.A2, CNY70-3.C, R21.Pin_1
  N4: Part1.A3, CNY70-4.C, R22.Pin_1
  N5: Part1.A4, CNY70-5.C, R23.Pin_1
  N6: Part1.A5, CNY70-6.C, R24.Pin_1
  N7: Part1.D21/SCL, Part2.SCL, Display1.SCL
  N8: Part1.D20/SDA, Part2.SDA, Display1.SDA
  GND: Part1.GND, Q1.source, R1.Pin_0, Q2.source, R3.Pin_0, Q5.source, Q6.source, R5.Pin_0, R6.Pin_0, Q7.source, Q11.source, Q12.source, R9.Pin_0, R11.Pin_0, R12.Pin_0, R2.Pin_0, Q4.source, Q3.source, R4.Pin_0, R13.Pin_1, R14.Pin_1, R15.Pin_1, R16.Pin_1, R17.Pin_1, R18.Pin_1, R19.Pin_0, R20.Pin_0, R21.Pin_0, R22.Pin_0, R23.Pin_0, R24.Pin_0, J1.pin1, S1.2, S2.2, S3.2, S4.2, Part2.GND, Display1.GND, R25.Pin_1, Reg1.OUT-
  5V: Part1.5V, CNY70-1.A, CNY70-1.E, CNY70-2.A, CNY70-2.E, CNY70-3.A, CNY70-3.E, CNY70-4.A, CNY70-4.E, CNY70-5.A, CNY70-5.E, CNY70-6.A, CNY70-6.E, Part2.Vin, Display1.VCC, Part3.5V
  N9: Part1.VIN, L1.pin2, L2.pin2, L3.pin2, L4.pin2, L5.pin2, L6.pin2, L7.pin2, L8.pin2, L9.pin2, L10.pin2, L11.pin2, L12.pin2, Reg1.OUT+
  N10: Part1.D2_PWM, S4.1
  N11: Part1.D3_PWM, S3.1
  N12: Part1.D4_PWM, S2.1
  N13: Part1.D5_PWM, S1.1
  N14: Part1.D6_PWM, J1.pin2
  N15: Part1.D7_PWM, LED1.anode
  N16: Part1.D23, Q1.gate, R1.Pin_1
  N17: Part1.D25, Q2.gate, R2.Pin_1
  N18: Part1.D27, Q3.gate, R4.Pin_1
  N19: Part1.D29, R3.Pin_1, Q4.gate
  N20: Part1.D31, Q5.gate, R6.Pin_1
  N21: Part1.D33, Q6.gate, R5.Pin_1
  N22: Part1.D35, Q10.gate, R8.Pin_1
  N23: Part1.D37, Q9.gate, R7.Pin_1
  N24: Part1.D39, Q8.gate, R10.Pin_1
  N25: Part1.D41, Q7.gate, R9.Pin_1
  N26: Part1.D43, Q11.gate, R11.Pin_1
  N27: Part1.D45, Q12.gate, R12.Pin_1
  N28: L1.pin1, Q1.drain
  N29: L2.pin1, Q2.drain
  N30: L3.pin1, Q3.drain
  N31: L4.pin1, Q4.drain
  N32: L5.pin1, Q5.drain
  N33: L6.pin1, Q6.drain
  N34: L7.pin1, Q9.drain
  N35: L8.pin1, Q10.drain
  N36: L9.pin1, Q8.drain
  N37: L10.pin1, Q12.drain
  N38: L11.pin1, Q11.drain
  N39: L12.pin1, Q7.drain
  N40: Q8.source, R10.Pin_0
  N41: Q9.source, R7.Pin_0
  N42: Q10.source, R8.Pin_0
  N43: CNY70-1.K, R13.Pin_0
  N44: CNY70-2.K, R14.Pin_0
  N45: CNY70-3.K, R15.Pin_0
  N46: CNY70-4.K, R16.Pin_0
  N47: CNY70-5.K, R17.Pin_0
  N48: CNY70-6.K, R18.Pin_0
  N49: LED1.cathode, R25.Pin_0
  N50: Reg1.IN-, U1.-, Part3.GND
  N51: Reg1.IN+, U1.+, Part3.VBAT

custom parts:
  CNY70: PHOTOTRANSISTOR
  Adafruit DS3231: The datasheet for the DS3231 explains that this part is an "Extremely Accurate I²C-Integrated RTC/TCXO/Crystal". And, hey, it does exactly what it says on the tin! This Real Time Clock (RTC) is the most precise you can get in a small, low power package. Most RTCs use an external 32kHz timing crystal that is used to keep time with low current draw. And that's all well and good, but those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
  LCD screen 16x2 IIC: LCD screen with HD44780 controller enables showing text, symbols, value or anything else that comes from Croduino/Arduino. It is capable of showing 16 symbols in two lines and therefore can be used in many projects that need to send clearly visible and legible output information.. • Color of symbols: White • Backlight: Blue • Dimensions: 80 x 36 x 12 mm • Screen dimensions: 64.5 x 16 mm •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
  DC-DC CONVERTER: WYHP 5A constant current/voltage manufactured by Shenzhen Weiyapuhua Technology Co., Ltd
  Micro Lipo Charger: Oh so handy, this little lipo charger is so small and easy to use you can keep it on your desk or mount it easily into any project! Simply plug it via any MicroUSB cable into a USB port and a 3.7V/4.2V lithium polymer or lithium ion rechargeable battery into the JST plug on the other end. There are two LEDs - one red and one green. While charging, the red LED is lit. When the battery is fully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
